// Logisim project VHDL_assignment2.circ as structural Verilog
module vhdl_hw2 (
  input  in_1,
  input  in_2,
  input  in_3,
  input  in_4,
  input  in_5,
  input  in_6,
  input  in_7,
  input  in_8,
  input  in_9,
  input  in_10,
  input  in_11,
  input  in_12,
  input  [2:0] in_13,
  input  in_14,
  input  [2:0] in_15,
  output out_16,
  output out_17,
  output out_18
);

  wire [7:0] seg_letter_1_display;

  logic4 logic4_1 (.a(in_1), .b(in_2), .c(in_3), .d(in_4), .out1(out_16), .out2(out_17));
  mux8_1 mux8_1_1 (
    .a(in_5), .b(in_6), .c(in_7), .d(in_8), .e(in_9), .f(in_10), .g(in_11), .h(in_12), .ch(in_13),
    .data(out_18));
  seg_letter seg_letter_1 (.en(in_14), .sel(in_15), .display(seg_letter_1_display));
  _7_Segment_Display u_7_segment_display_1 (
    .g(seg_letter_1_display[1]), .f(seg_letter_1_display[2]), .a(seg_letter_1_display[7]),
    .b(seg_letter_1_display[6]), .e(seg_letter_1_display[3]), .d(seg_letter_1_display[4]),
    .c(seg_letter_1_display[5]), .dp(seg_letter_1_display[0]));
endmodule

// VHDL entity logic4, as the project stores it:
library ieee;
use ieee.std_logic_1164.all;

entity logic4 is
    port(
        a,b,c,d  :in  std_logic;
        out1,out2:out std_logic
    );
end entity logic4;

architecture bhv of logic4 is
begin
    out1 <= a and b and c and d;
    out2 <= a or b or c or d;
end architecture bhv;

// VHDL entity mux8_1, as the project stores it:
library ieee;
use ieee.std_logic_1164.all;

entity mux8_1 is
    port(
        a,b,c,d,e,f,g,h :in  std_logic;
        ch              :in  std_logic_vector(2 downto 0);
        data            :out std_logic
    );
end entity mux8_1;

architecture bhv of mux8_1 is
begin
    process(a,b,c,d,e,f,g,h,ch)
    begin
        case ch is
            when "000" => data <= a;
            when "001" => data <= b;
            when "010" => data <= c;
            when "011" => data <= d;
            when "100" => data <= e;
            when "101" => data <= f;
            when "110" => data <= g;
            when "111" => data <= h;
            when others => data <= '0';
        end case;
    end process;
end architecture bhv;

// VHDL entity seg_letter, as the project stores it:
library ieee;
use ieee.std_logic_1164.all;

entity seg_letter is
    port(
        en      :in  std_logic;
        sel     :in  std_logic_vector(2 downto 0);
        display :out std_logic_vector(7 downto 0)  -- a b c d e f g dp
    );
end entity seg_letter;

architecture bhv of seg_letter is
begin
    process(en, sel)
    begin
        if en = '0' then
            display <= "ZZZZZZZZ";
        else
            case sel is
                when "000" => display <= "11101110"; -- A
                when "001" => display <= "00111110"; -- b
                when "010" => display <= "10011100"; -- C
                when "011" => display <= "01111010"; -- d
                when "100" => display <= "10001110"; -- F
                when "101" => display <= "10111100"; -- G
                when others => display <= "00000000";
            end case;
        end if;
    end process;
end architecture bhv;
